// Logisim project adder.circ as structural Verilog: 1 circuit, main circuit main
module main (
);

  wire and_1_out, and_2_out, or_1_out, xor_1_out, xor_2_out;

  xor xor_1 (xor_1_out, 1'b1, 1'b1);
  and and_1 (and_1_out, 1'b0, xor_1_out);
  and and_2 (and_2_out, 1'b1, 1'b1);
  xor xor_2 (xor_2_out, xor_1_out, 1'b0);
  or or_1 (or_1_out, and_1_out, and_2_out);

  // Notes on the sheet:
  //   carry in
  //   a
  //   b
  //   sum
  //   carry out
endmodule
