// Logisim project counter.circ as structural Verilog: 1 circuit, main circuit main
module main (
);

  wire and_1_out, and_2_out, and_3_out, and_4_out, button_1_out, j_k_ff_1_q, j_k_ff_1_qn, j_k_ff_2_q,
       not_1_out, not_2_out;

  Button button_1 (.out(button_1_out));
  and and_1 (and_1_out, 1'b1, 1'b0);
  J_K_Flip_Flop j_k_ff_1 (
    .J(1'b1), .clk(button_1_out), .K(1'b1), .Q(j_k_ff_1_q), .Qn(j_k_ff_1_qn), .preset(and_1_out),
    .reset(and_2_out));  // open: en
  and and_2 (and_2_out, 1'b1, not_1_out);
  not not_1 (not_1_out, 1'b0);
  J_K_Flip_Flop j_k_ff_2 (
    .J(1'b1), .clk(j_k_ff_1_qn), .K(1'b1), .Q(j_k_ff_2_q), .preset(and_3_out), .reset(and_4_out));  // open: Qn, en
  and and_3 (and_3_out, 1'b1, 1'b1);
  and and_4 (and_4_out, 1'b1, not_2_out);
  not not_2 (not_2_out, 1'b1);

  // Notes on the sheet:
  //   we
  //   increment
  //   data out
  //   data in
endmodule
