// Logisim project cpu.circ as structural Verilog: 5 circuits, main circuit main
module main (
);

  wire button_1_out;
  wire [7:0] adder_1_out, multiplexer_1_out, multiplexer_2_out, ram_1_data, register_1_q, register_2_q,
       register_3_q, register_4_q, register_6_q;

  Button button_1 (.out(button_1_out));
  Register register_1 (.D(multiplexer_2_out), .en(1'b0), .Q(register_1_q), .clk(button_1_out));  // open: clr
  Register register_2 (.D(multiplexer_2_out), .en(1'b1), .Q(register_2_q), .clk(button_1_out));  // open: clr
  Register register_3 (.D(multiplexer_2_out), .en(1'b0), .Q(register_3_q), .clk(button_1_out));  // open: clr
  Register register_4 (.D(multiplexer_2_out), .en(1'b0), .Q(register_4_q), .clk(button_1_out));  // open: clr
  Register register_5 (.D(multiplexer_2_out), .en(1'b0), .clk(button_1_out));  // open: Q, clr
  RAM #(.bus("separate")) ram_1 (
    .addr(multiplexer_1_out), .din(multiplexer_2_out), .data(ram_1_data), .str(1'b0), .clk(button_1_out));  // open: sel, ld, clr
  Adder adder_1 (.a(register_1_q), .b(register_2_q), .out(adder_1_out));  // open: cin, cout
  Register register_6 (.D(adder_1_out), .Q(register_6_q), .clk(button_1_out));  // open: en, clr
  Multiplexer #(.select(3), .width(8), .enable("false")) multiplexer_1 (
    .in0(ram_1_data), .in1(register_1_q), .in2(register_6_q), .in3(register_2_q), .in4(register_3_q),
    .in5(register_4_q), .out(multiplexer_1_out), .sel(3'b100));  // open: in6, in7
  Multiplexer #(.select(3), .width(8), .enable("false")) multiplexer_2 (
    .in0(ram_1_data), .in1(register_1_q), .in2(register_6_q), .in3(register_2_q), .in4(register_3_q),
    .in5(register_4_q), .out(multiplexer_2_out), .sel(3'b101));  // open: in6, in7

  // Notes on the sheet:
  //   Register A
  //   Register B
  //   Memory
  //   Program counter
  //   Operand register
  //   Instruction register
  //   ALU
endmodule

module sequence_generator (
  input  clk,
  input  reset,
  output FETCH_INSTRUCTION_LOAD,
  output FETCH_INSTRUCTION_STORE,
  output FETCH_OPERAND_LOAD,
  output FETCH_OPERAND_STORE,
  output EXECUTE_LOAD,
  output EXECUTE_STORE
);

  wire nor_1_out, or_1_out, shift_register_1_out;

  main main_1 ();
  or or_1 (or_1_out, shift_register_1_out, nor_1_out);
  Shift_Register #(.length(6)) shift_register_1 (
    .in(or_1_out), .clk(clk), .out(shift_register_1_out), .clr(reset), .q0(FETCH_INSTRUCTION_LOAD),
    .q1(FETCH_INSTRUCTION_STORE), .q2(FETCH_OPERAND_LOAD), .q3(FETCH_OPERAND_STORE), .q4(EXECUTE_LOAD),
    .q5(EXECUTE_STORE));  // open: shift, load, d0, d1, d2, d3, d4, d5
  nor nor_1 (nor_1_out, FETCH_INSTRUCTION_LOAD, FETCH_INSTRUCTION_STORE, FETCH_OPERAND_LOAD, FETCH_OPERAND_STORE, EXECUTE_LOAD, EXECUTE_STORE);
endmodule

module cpu (
  output [7:0] out_1,
  output [7:0] out_2,
  output [2:0] out_3,
  output [7:0] out_4,
  output [2:0] out_5
);

  wire alu_we, and_1_out, clk, instr_we, mem_we, operand_we, pc_inc, pc_we, reg_a_we, reg_b_we, reset;
  wire [7:0] adder_1_out, alu_out, counter_1_q, instr, register_1_q, register_2_q, register_3_q;

  Button button_1 (.out(clk));
  Button button_2 (.out(reset));
  and and_1 (and_1_out, ~alu_out[0], ~alu_out[1], ~alu_out[2], ~alu_out[3], ~alu_out[4], ~alu_out[5], ~alu_out[6], ~alu_out[7]);  // AND_Gate
  Register register_1 (.D(out_4), .en(reg_a_we), .Q(register_1_q), .clk(clk), .clr(reset));
  Register register_2 (.D(out_4), .en(reg_b_we), .Q(register_2_q), .clk(clk), .clr(reset));
  Counter counter_1 (.load(pc_we), .D(out_4), .count(pc_inc), .Q(counter_1_q), .clk(clk), .clr(reset));  // open: carry
  Register register_3 (.D(out_4), .en(operand_we), .Q(register_3_q), .clk(clk), .clr(reset));
  Register register_4 (.D(out_4), .en(instr_we), .Q(instr), .clk(clk), .clr(reset));
  controller2 controller2_1 (
    .clk(clk), .reset(reset), .alu_zero(and_1_out), .instr_reg_value(instr), .addr_mux_sel(out_3),
    .value_mux_sel(out_5), .mem_we(mem_we), .reg_a_we(reg_a_we), .pc_we(pc_we), .reg_b_we(reg_b_we),
    .pc_inc(pc_inc), .reg_alu_we(alu_we), .operand_we(operand_we), .instruction_we(instr_we));
  RAM #(.bus("separate")) ram_1 (
    .addr(out_2), .din(out_4), .data(out_1), .str(mem_we), .clk(clk));  // open: sel, ld, clr
  Adder adder_1 (.a(register_1_q), .b(register_2_q), .out(adder_1_out));  // open: cin, cout
  Register register_5 (.D(adder_1_out), .en(alu_we), .Q(alu_out), .clk(clk), .clr(reset));
  Multiplexer #(.select(3), .width(8), .enable("false")) multiplexer_1 (
    .in0(out_1), .in1(register_1_q), .in2(alu_out), .in3(register_2_q), .in4(counter_1_q),
    .in5(register_3_q), .out(out_2), .sel(out_3));  // open: in6, in7
  Multiplexer #(.select(3), .width(8), .enable("false")) multiplexer_2 (
    .in0(out_1), .in1(register_1_q), .in2(alu_out), .in3(register_2_q), .in4(counter_1_q),
    .in5(register_3_q), .out(out_4), .sel(out_5));  // open: in6, in7

  // Other names for the same wires on the sheet: addr_mux_sel[2:0] = out_3; data_mux_sel[2:0] = out_5

  // Notes on the sheet:
  //   Register A
  //   Register B
  //   Memory
  //   Program counter
  //   Operand register
  //   Instruction register
  //   ALU
endmodule

module shift_register (
);

  wire button_1_out, d_ff_1_q, d_ff_2_q, d_ff_3_q;

  Button button_1 (.out(button_1_out));
  D_Flip_Flop d_ff_1 (.clk(button_1_out), .D(1'b0), .Q(d_ff_1_q));  // open: Qn, preset, en, reset
  D_Flip_Flop d_ff_2 (.clk(button_1_out), .D(d_ff_1_q), .Q(d_ff_2_q));  // open: Qn, preset, en, reset
  D_Flip_Flop d_ff_3 (.clk(button_1_out), .D(d_ff_2_q), .Q(d_ff_3_q));  // open: Qn, preset, en, reset
  D_Flip_Flop d_ff_4 (.clk(button_1_out), .D(d_ff_3_q));  // open: Q, Qn, preset, en, reset
endmodule

module controller2 (
  input  clk,
  input  reset,
  input  alu_zero,
  input  [7:0] instr_reg_value,
  output [2:0] addr_mux_sel,
  output [2:0] value_mux_sel,
  output mem_we,
  output reg_a_we,
  output pc_we,
  output reg_b_we,
  output pc_inc,
  output reg_alu_we,
  output operand_we,
  output instruction_we
);

  wire and_6_out, COND, EXECUTE_LOAD, EXECUTE_STORE, FETCH_I_LOAD, FETCH_O_LOAD, MEM_TO_REG, or_1_out,
       or_2_out, or_3_out, or_4_out, or_5_out, or_6_out, or_7_out, REG_TO_MEM, REG_TO_REG;
  wire [1:0] and_5_out;

  sequence_generator sequence_generator_1 (
    .clk(clk), .reset(reset), .FETCH_INSTRUCTION_LOAD(FETCH_I_LOAD),
    .FETCH_INSTRUCTION_STORE(instruction_we), .FETCH_OPERAND_LOAD(FETCH_O_LOAD),
    .FETCH_OPERAND_STORE(operand_we), .EXECUTE_LOAD(EXECUTE_LOAD), .EXECUTE_STORE(EXECUTE_STORE));
  Decoder #(.select(2)) decoder_1 (
    .out0(REG_TO_REG), .out1(REG_TO_MEM), .out2(MEM_TO_REG), .out3(COND), .sel(instr_reg_value[7:6]));  // open: en
  or or_1 (or_1_out, REG_TO_REG, MEM_TO_REG);
  or or_2 (or_2_out, REG_TO_REG, MEM_TO_REG);
  or or_3 (or_3_out, REG_TO_REG, MEM_TO_REG);
  and and_1 (reg_a_we, instr_reg_value[0], EXECUTE_STORE, or_1_out);
  and and_2 (reg_b_we, instr_reg_value[1], EXECUTE_STORE, or_2_out);
  and and_3 (reg_alu_we, instr_reg_value[2], EXECUTE_STORE, or_3_out);
  or or_4 (or_4_out, REG_TO_REG, REG_TO_MEM);
  or or_5 (or_5_out, EXECUTE_LOAD, EXECUTE_STORE);
  or or_6 (or_6_out, REG_TO_MEM, MEM_TO_REG);
  or or_7 (or_7_out, EXECUTE_LOAD, EXECUTE_STORE);
  and and_4 (and_5_out[1], or_4_out, or_5_out);
  and and_5 (and_5_out[0], or_5_out, REG_TO_REG);
  and and_6 (and_6_out, or_6_out, or_7_out);
  Multiplexer #(.width(3)) multiplexer_1 (
    .in0(3'b100), .in1(instr_reg_value[5:3]), .out(addr_mux_sel), .sel(and_6_out));  // open: en
  Multiplexer #(.select(2), .width(3)) multiplexer_2 (
    .in0(3'b000), .in2(instr_reg_value[2:0]), .in3(instr_reg_value[5:3]), .out(value_mux_sel), .sel(and_5_out));  // open: in1, en
  and and_7 (mem_we, REG_TO_MEM, EXECUTE_STORE);
  and and_8 (pc_we, COND, EXECUTE_STORE, alu_zero);
  or or_8 (pc_inc, instruction_we, operand_we);

  // Other names for the same wires on the sheet: FETCH_I_STORE = instruction_we; FETCH_O_STORE = operand_we;
  //   instr_0 = instr_reg_value[0]; suboperand_0[2:0] = instr_reg_value[2:0]; instr_1 = instr_reg_value[1];
  //   instr_2 = instr_reg_value[2]; suboperand_1[2:0] = instr_reg_value[5:3]
endmodule
