// Logisim project cpu_blocks_no_control.circ as structural Verilog: 1 circuit, main circuit main
module main (
);

  wire button_1_out;
  wire [7:0] adder_1_out, multiplexer_1_out, multiplexer_2_out, ram_1_data, register_1_q, register_2_q,
       register_3_q, register_4_q, register_5_q, register_6_q;

  Button button_1 (.out(button_1_out));
  Register register_1 (.D(multiplexer_2_out), .en(1'b0), .Q(register_1_q), .clk(button_1_out));  // open: clr
  Register register_2 (.D(multiplexer_2_out), .en(1'b0), .Q(register_2_q), .clk(button_1_out));  // open: clr
  Register register_3 (.D(multiplexer_2_out), .en(1'b0), .Q(register_3_q), .clk(button_1_out));  // open: clr
  Register register_4 (.D(multiplexer_2_out), .en(1'b0), .Q(register_4_q), .clk(button_1_out));  // open: clr
  Register register_5 (.D(multiplexer_2_out), .en(1'b1), .Q(register_5_q), .clk(button_1_out));  // open: clr
  RAM #(.bus("separate")) ram_1 (
    .addr(multiplexer_1_out), .din(multiplexer_2_out), .data(ram_1_data), .str(1'b0), .clk(button_1_out));  // open: sel, ld, clr
  Adder adder_1 (.a(register_1_q), .b(register_2_q), .out(adder_1_out));  // open: cin, cout
  Register register_6 (.D(adder_1_out), .en(1'b0), .Q(register_6_q), .clk(button_1_out));  // open: clr
  Multiplexer #(.select(3), .width(8), .enable("false")) multiplexer_1 (
    .in0(ram_1_data), .in1(register_1_q), .in2(register_6_q), .in3(register_2_q), .in4(register_3_q),
    .in5(register_4_q), .out(multiplexer_1_out), .sel(3'b100));  // open: in6, in7
  Multiplexer #(.select(3), .width(8), .enable("false")) multiplexer_2 (
    .in0(ram_1_data), .in1(register_1_q), .in2(register_6_q), .in3(register_2_q), .in4(register_3_q),
    .in5(register_4_q), .out(multiplexer_2_out), .sel(3'b000));  // open: in6, in7

  // Notes on the sheet:
  //   Register A
  //   Register B
  //   Memory
  //   Program counter
  //   Operand register
  //   Instruction register
  //   ALU
endmodule
