// Logisim project d-flip-flop.circ as structural Verilog: 1 circuit, main circuit main
module main (
);

  wire and_1_out, and_2_out, and_3_out, nor_1_out, nor_2_out, not_1_out;

  and and_1 (and_1_out, 1'b0, 1'b0);
  not not_1 (not_1_out, 1'b0);
  and and_2 (and_2_out, not_1_out, and_1_out);
  and and_3 (and_3_out, and_1_out, 1'b0);
  nor nor_1 (nor_1_out, and_2_out, nor_2_out);
  nor nor_2 (nor_2_out, nor_1_out, and_3_out);

  // Notes on the sheet:
  //   data
  //   write enable
  //   clock
  //   output
endmodule
