// Logisim project edge-triggered-jk-flip-lfop.circ as structural Verilog: 1 circuit, main circuit main
module main (
);

  wire nand_1_out, nand_2_out, nand_3_out, nand_4_out, nand_5_out, nand_6_out, nand_7_out, nand_8_out,
       not_1_out, not_2_out;

  not not_1 (not_1_out, 1'b1);
  nand nand_1 (nand_1_out, nand_8_out, 1'b1, not_1_out);
  nand nand_2 (nand_2_out, not_1_out, 1'b1, nand_7_out);
  not not_2 (not_2_out, not_1_out);
  nand nand_3 (nand_3_out, nand_1_out, nand_4_out);
  nand nand_4 (nand_4_out, nand_3_out, nand_2_out);
  nand nand_5 (nand_5_out, nand_3_out, not_2_out);
  nand nand_6 (nand_6_out, not_2_out, nand_4_out);
  nand nand_7 (nand_7_out, nand_5_out, nand_8_out);
  nand nand_8 (nand_8_out, nand_7_out, nand_6_out);

  // Notes on the sheet:
  //   J input
  //   clock input
  //   K input
  //   J = 0, K = 0, rising edge -> nothing
  //   J = 1 K = 0, rising edge output -> 1
  //   J = 0, K = 1, rising edge output -> 0
  //   J =1, K =1, rising edge output -> toggle
  //   output
  //   inverted output
endmodule
