// Logisim project mux.circ as structural Verilog: 1 circuit, main circuit main
module main (
);

  wire and_1_out, and_2_out, and_3_out, and_4_out, not_1_out, not_2_out, or_1_out;

  not not_1 (not_1_out, 1'b0);
  not not_2 (not_2_out, 1'b0);
  and and_1 (and_1_out, 1'b1, not_1_out, not_2_out);
  and and_2 (and_2_out, 1'b1, 1'b0, not_2_out);
  and and_3 (and_3_out, 1'b0, not_1_out, 1'b0);
  and and_4 (and_4_out, 1'b1, 1'b0, 1'b0);
  or or_1 (or_1_out, and_1_out, and_2_out, and_3_out, and_4_out);

  // Notes on the sheet:
  //   in1
  //   in2
  //   in3
  //   in4
  //   Inverters
  //   sel1
  //   sel2
  //   And gates
  //   Or gate
  //   out
endmodule
