// Logisim project mux2.circ as structural Verilog: 1 circuit, main circuit main
module main (
);

  wire multiplexer_1_out, multiplexer_2_out, multiplexer_3_out, multiplexer_4_out;

  Multiplexer #(.select(2)) multiplexer_1 (
    .in0(1'b1), .in1(1'b0), .in2(1'b0), .in3(1'b0), .out(multiplexer_1_out), .sel(2'b01));  // open: en
  Multiplexer #(.select(2)) multiplexer_2 (
    .in0(1'b0), .in1(1'b1), .in2(1'b0), .in3(1'b0), .out(multiplexer_2_out), .sel(2'b01));  // open: en
  Multiplexer #(.select(2)) multiplexer_3 (
    .in0(1'b0), .in1(1'b0), .in2(1'b1), .in3(1'b0), .out(multiplexer_3_out), .sel(2'b01));  // open: en
  Multiplexer #(.select(2)) multiplexer_4 (
    .in0(1'b0), .in1(1'b0), .in2(1'b0), .in3(1'b1), .out(multiplexer_4_out), .sel(2'b01));  // open: en

  // Notes on the sheet:
  //   4 bit intput 0
  //   4 bit intput 1
  //   4 bit input 2
  //   4 bit input 3
  //   selector
  //   4 bit output
endmodule
