// Logisim project register2.circ as structural Verilog: 1 circuit, main circuit main
module main (
);

  wire d_ff_1_q, d_ff_2_q, d_ff_3_q, d_ff_4_q;

  D_Flip_Flop d_ff_1 (.clk(1'b1), .D(1'b0), .Q(d_ff_1_q), .en(1'b0), .reset(1'b0));  // open: Qn, preset
  D_Flip_Flop d_ff_2 (.clk(1'b1), .D(1'b0), .Q(d_ff_2_q), .en(1'b0), .reset(1'b0));  // open: Qn, preset
  D_Flip_Flop d_ff_3 (.clk(1'b1), .D(1'b0), .Q(d_ff_3_q), .en(1'b0), .reset(1'b0));  // open: Qn, preset
  D_Flip_Flop d_ff_4 (.clk(1'b1), .D(1'b0), .Q(d_ff_4_q), .en(1'b0), .reset(1'b0));  // open: Qn, preset

  // Notes on the sheet:
  //   write enable
  //   clock
  //   clear
  //   4 bit output
  //   4 bit input
endmodule
