// Logisim project sequence_generator.circ as structural Verilog: 1 circuit, main circuit main
module main (
);

  wire button_1_out, nor_1_out, or_1_out, shift_register_1_out, shift_register_1_q0, shift_register_1_q1,
       shift_register_1_q2, shift_register_1_q3, shift_register_1_q4, shift_register_1_q5;

  or or_1 (or_1_out, shift_register_1_out, nor_1_out);
  Button button_1 (.out(button_1_out));
  Shift_Register #(.length(6)) shift_register_1 (
    .in(or_1_out), .clk(button_1_out), .out(shift_register_1_out), .q0(shift_register_1_q0),
    .q1(shift_register_1_q1), .q2(shift_register_1_q2), .q3(shift_register_1_q3), .q4(shift_register_1_q4),
    .q5(shift_register_1_q5));  // open: shift, load, clr, d0, d1, d2, d3, d4, d5
  nor nor_1 (nor_1_out, shift_register_1_q0, shift_register_1_q1, shift_register_1_q2, shift_register_1_q3, shift_register_1_q4, shift_register_1_q5);

  // Notes on the sheet:
  //   FETCH_INSTRUCTION_LOAD
  //   FETCH_INSTRUCTION_STORE
  //   FETCH_OPERAND_LOAD
  //   FETCH_OPERAND_STORE
  //   EXECUTE_STORE
  //   EXECUTE_LOAD
endmodule
